# Fritzing sketch project (saved by Fritzing 0.9.6b)
breadboards: 1

parts:
  J1 = STM32 Nucleo boards
  R1 = Resistor [tolerance=±5% power=0.25 resistance=150 package=THT]
  LED1 = LED - 5mm [color="Red (633nm)" current=0.030 package="5 mm [THT]"]
  J2 = Infrared Proximity Sensor

nets:
  N1: J1.PC8, J2.Vout
  N2: J1.PC5, R1.Pin_0
  N3: J1.GND#229, LED1.cathode, J2.GND
  5V: J1.5V, J2.Vcc
  N4: J1.CN_01, J1.CN_02
  N5: J1.CN_03, J1.CN_04
  N6: J1.GND#880, J1.GND#881
  N7: J1.GND#1149, J1.GND#1150
  N8: R1.Pin_1, LED1.anode
