# Fritzing sketch anim (saved by Fritzing 0.9.6b)
breadboards: 1

parts:
  J1 = STM32 Nucleo boards
  LED1 = LED - 5mm [color="Blue (430nm)" current=0.030 package="5 mm [THT]"]
  R1 = Resistor [tolerance=±5% resistance=150 package="2512 [SMD]"]

nets:
  N1: J1.GND, LED1.cathode
  N2: J1.PA5, R1.Pin_0
  N3: LED1.anode, R1.Pin_1
